// Logisim project ALU.circ as structural Verilog: 8 circuits, main circuit main
module main (
  input  [3:0] Selector,
  input  [31:0] In1,
  input  [31:0] In2,
  output Carry,
  output [31:0] Output,
  output ZF,
  output SF,
  output [31:0] Remainder
);

  wire C, C_t, sf_1_out_2;
  wire [31:0] AND, Carry_DIVU, Carry_MULU, Carry_t, Carry_X, DIVU, MULU, NOR, OR, Out, Out_minus, Out_plus,
       Out_star, SLT, SLTU, XOR;

  Adder #(.width(32)) adder_1 (.a(In1), .b(In2), .out(Out_plus), .cin(1'b0), .cout(C));
  Subtractor #(.width(32)) subtractor_1 (.a(In1), .b(In2), .out(Out_minus), .bin(1'b0), .bout(C_t));
  Multiplier #(.width(32)) multiplier_1 (.a(In1), .b(In2), .out(Out_star), .cout(Carry_X));  // open: cin
  MULU mulu_1 (.in_1(In1), .in_2(In2), .Output(MULU), .Carry_Out(Carry_MULU));
  Divider #(.width(32)) divider_1 (.a(In1), .b(In2), .out(Out), .rem(Carry_t));  // open: upper
  DIVU divu_1 (.in_1(In1), .in_2(In2), .Output(DIVU), .Remainder(Carry_DIVU));
  assign AND = In1 & In2;  // AND_Gate and_1, 32 bits wide
  assign NOR = ~(In1 | In2);  // NOR_Gate nor_1, 32 bits wide
  assign OR = In1 | In2;  // OR_Gate or_1, 32 bits wide
  assign XOR = In1 ^ In2;  // XOR_Gate xor_1, 32 bits wide
  SLT slt_1 (.in_1(In1), .in_2(In2), .out_3(SLT));
  SLTU sltu_1 (.in_1(In1), .in_2(In2), .Output(SLTU));
  Multiplexer #(.select(4), .width(32), .enable("false")) multiplexer_1 (
    .in2(Carry_X), .in3(Carry_t), .in9(Carry_MULU), .in10(Carry_DIVU), .out(Remainder), .sel(Selector));  // open: in0, in1, in4, in5, in6, in7, in8, in11, in12, in13, in14, in15
  Multiplexer #(.select(4), .width(32), .enable("false")) multiplexer_2 (
    .in0(Out_plus), .in1(Out_minus), .in2(Out_star), .in3(Out), .in4(AND), .in5(NOR), .in6(OR), .in7(XOR),
    .in8(SLT), .in9(MULU), .in10(DIVU), .in11(SLTU), .out(Output), .sel(Selector));  // open: in12, in13, in14, in15
  Multiplexer #(.select(4)) multiplexer_3 (
    .in0(C), .in1(C_t), .in2(1'b0), .in3(1'b0), .in4(1'b0), .in5(1'b0), .in6(1'b0), .in7(1'b0), .in8(1'b0),
    .in9(1'b0), .out(Carry), .sel(Selector));  // open: in10, in11, in12, in13, in14, in15, en
  ZF zf_1 (.in_1(Output), .out_2(ZF));
  SF sf_1 (.in_1(Output), .out_2(sf_1_out_2));
  not not_1 (SF, sf_1_out_2);

  // Other names for the same wires on the sheet: _1[31:0] = In1; _2[31:0] = In2
endmodule

module SLT (
  input  [31:0] in_1,
  input  [31:0] in_2,
  output [31:0] out_3
);

  wire comparator_1_lt;

  Comparator #(.width(32)) comparator_1 (.a(in_1), .b(in_2), .lt(comparator_1_lt));  // open: gt, eq
  Multiplexer #(.width(32), .enable("false")) multiplexer_1 (
    .in0({32{1'b0}}), .in1(32'h1), .out(out_3), .sel(comparator_1_lt));
endmodule

module ZF (
  input  [31:0] in_1,
  output out_2
);

  wire or_1_out;

  or or_1 (or_1_out, in_1[0], in_1[1], in_1[2], in_1[3], in_1[4], in_1[5], in_1[6], in_1[7], in_1[8], in_1[9], in_1[10], in_1[11], in_1[12], in_1[13], in_1[14], in_1[15], in_1[16], in_1[17], in_1[18], in_1[19], in_1[20], in_1[21], in_1[22], in_1[23], in_1[24], in_1[25], in_1[26], in_1[27], in_1[28], in_1[29], in_1[30], in_1[31]);
  not not_1 (out_2, or_1_out);
endmodule

module SF (
  input  [31:0] in_1,
  output out_2
);

  Comparator #(.width(32)) comparator_1 (.a(in_1), .b({32{1'b0}}), .gt(out_2));  // open: eq, lt
endmodule

module MULU (
  input  [31:0] in_1,
  input  [31:0] in_2,
  output [31:0] Output,
  output [31:0] Carry_Out
);

  wire Out_1, Out_2;
  wire [31:0] IN_1_t, IN_2_t, negator_1_out, negator_2_out;

  and and_1 (Out_1, in_1[31], 1'b1);
  and and_2 (Out_2, in_2[31], 1'b1);
  Negator #(.width(32)) negator_1 (.in(in_1), .out(negator_1_out));
  Negator #(.width(32)) negator_2 (.in(in_2), .out(negator_2_out));
  Multiplier #(.width(32)) multiplier_1 (.a(IN_1_t), .b(IN_2_t), .out(Output), .cout(Carry_Out));  // open: cin
  Multiplexer #(.width(32), .enable("false")) multiplexer_1 (
    .in0(in_1), .in1(negator_1_out), .out(IN_1_t), .sel(Out_1));
  Multiplexer #(.width(32), .enable("false")) multiplexer_2 (
    .in0(in_2), .in1(negator_2_out), .out(IN_2_t), .sel(Out_2));

  // Other names for the same wires on the sheet: _1[31:0] = in_1; bit_31__1 = in_1[31]; _2[31:0] = in_2;
  //   bit_31__2 = in_2[31]
endmodule

module DIVU (
  input  [31:0] in_1,
  input  [31:0] in_2,
  output [31:0] Output,
  output [31:0] Remainder
);

  wire Out_1, Out_2;
  wire [31:0] IN_1_t, IN_2_t, negator_1_out, negator_2_out;

  and and_1 (Out_1, in_1[31], 1'b1);
  and and_2 (Out_2, in_2[31], 1'b1);
  Negator #(.width(32)) negator_1 (.in(in_1), .out(negator_1_out));
  Negator #(.width(32)) negator_2 (.in(in_2), .out(negator_2_out));
  Divider #(.width(32)) divider_1 (.a(IN_1_t), .b(IN_2_t), .out(Output), .rem(Remainder));  // open: upper
  Multiplexer #(.width(32), .enable("false")) multiplexer_1 (
    .in0(in_1), .in1(negator_1_out), .out(IN_1_t), .sel(Out_1));
  Multiplexer #(.width(32), .enable("false")) multiplexer_2 (
    .in0(in_2), .in1(negator_2_out), .out(IN_2_t), .sel(Out_2));

  // Other names for the same wires on the sheet: _1[31:0] = in_1; bit_31__1 = in_1[31]; _2[31:0] = in_2;
  //   bit_31__2 = in_2[31]
endmodule

module SLTU (
  input  [31:0] in_1,
  input  [31:0] in_2,
  output [31:0] Output
);

  wire Out_1, Out_2;
  wire [31:0] IN_1_t, IN_2_t, negator_1_out, negator_2_out;

  and and_1 (Out_1, in_1[31], 1'b1);
  and and_2 (Out_2, in_2[31], 1'b1);
  Negator #(.width(32)) negator_1 (.in(in_1), .out(negator_1_out));
  Negator #(.width(32)) negator_2 (.in(in_2), .out(negator_2_out));
  SLT slt_1 (.in_1(IN_1_t), .in_2(IN_2_t), .out_3(Output));
  Multiplexer #(.width(32), .enable("false")) multiplexer_1 (
    .in0(in_1), .in1(negator_1_out), .out(IN_1_t), .sel(Out_1));
  Multiplexer #(.width(32), .enable("false")) multiplexer_2 (
    .in0(in_2), .in1(negator_2_out), .out(IN_2_t), .sel(Out_2));

  // Other names for the same wires on the sheet: _1[31:0] = in_1; bit_31__1 = in_1[31]; _2[31:0] = in_2;
  //   bit_31__2 = in_2[31]
endmodule

module Branch_Control_Unit (
  input  in_1,
  input  in_2,
  input  [15:0] in_3
);


  // Other names for the same wires on the sheet: Offset[15:0] = in_3; SF = in_2; ZF = in_1
endmodule
