// Logisim project Control Unit.circ as structural Verilog: 1 circuit, main circuit Control Unit
module Control_Unit (
  input  in_1,
  input  in_2,
  input  in_3,
  input  in_4,
  input  in_5,
  input  in_6,
  input  in_7,
  input  in_8,
  input  in_9,
  input  in_10,
  input  in_11,
  input  in_12,
  input  in_13,
  input  in_14,
  input  in_15,
  input  in_16,
  input  in_17,
  input  in_18,
  input  in_19,
  input  in_20,
  input  in_21,
  input  in_22,
  input  in_23,
  input  in_24,
  input  in_25,
  input  in_26,
  input  in_27,
  input  in_28,
  input  in_29,
  input  in_30,
  input  in_31,
  input  in_32,
  input  in_33,
  input  in_34,
  input  in_35,
  input  in_36,
  input  in_37,
  input  in_38,
  input  in_39,
  output out_40,
  output out_41,
  output out_42,
  output out_43,
  output out_44,
  output out_45,
  output out_46,
  output ALU_flag,
  output [3:0] ALU_op,
  output ALU_sign,
  output stack_flag,
  output pop_push_flag,
  output enable_pop,
  output enable_push,
  output out_54,
  output out_55
);

  wire A_add, A_addi, A_and, A_andi, A_beq, A_bgtz, A_blez, A_bltz, A_bne, A_div, A_divu, A_jr, A_jump, A_lw,
       A_mfhi, A_mflo, A_mult, A_mulu, A_nop, A_nor, A_or, A_ori, A_pop, A_push, A_slt, A_slti, A_sltiu,
       A_sltu, A_sub, A_sw, A_xor, A_xori, and_33_out, and_34_out, and_36_out, and_37_out, and_39_out,
       and_43_out, d_ff_1_q, d_ff_1_qn, demultiplexer_1_out0, demultiplexer_1_out1, nand_1_out, nor_1_out,
       operation, or_4_out, or_5_out, or_6_out, or_7_out, or_8_out, or_9_out, or_11_out, or_12_out,
       or_15_out, or_16_out, undriven;
  wire [3:0] priority_encoder_1_out;

  and and_1 (A_nop, operation, in_1);
  and and_2 (A_mulu, operation, in_2);
  and and_3 (A_sltu, operation, in_3);
  and and_4 (A_xor, operation, in_4);
  and and_5 (A_jr, operation, in_6);
  and and_6 (out_45, operation, in_7);
  and and_7 (A_addi, operation, in_8);
  and and_8 (A_ori, operation, in_9);
  or or_1 (ALU_flag, in_13, in_22, in_30, in_14, in_15, in_34, in_24, in_4, in_32, in_2, in_23, in_3);
  or or_2 (ALU_sign, A_mult, A_div, A_slt);
  or or_3 (out_54, A_sub, A_mulu, A_or, A_bltz, A_bne, A_xori, A_and, A_andi, A_nor, A_div, A_mult, A_divu, A_xor, A_addi, A_ori, A_beq, A_blez, A_bgtz, A_add);
  and and_9 (A_beq, operation, in_10);
  and and_10 (A_bltz, operation, in_11);
  and and_11 (A_jump, operation, in_12);
  and and_12 (A_add, operation, in_13);
  and and_13 (A_div, operation, in_14);
  and and_14 (A_and, operation, in_15);
  and and_15 (A_mfhi, operation, in_17);
  and and_16 (out_43, operation, in_18);
  or or_4 (or_4_out, in_15, in_37);
  or or_5 (or_5_out, in_4, in_20);
  or or_6 (or_6_out, in_27, in_3);
  or or_7 (or_7_out, in_13, in_8, in_28, in_38);
  or or_8 (or_8_out, in_24, in_9);
  or or_9 (or_9_out, in_32, in_19);
  and and_17 (A_slti, operation, in_19);
  and and_18 (A_xori, operation, in_20);
  and and_19 (A_bne, operation, in_21);
  and and_20 (A_sub, operation, in_22);
  and and_21 (A_divu, operation, in_23);
  and and_22 (A_or, operation, in_24);
  and and_23 (A_mflo, operation, in_25);
  and and_24 (out_55, operation, in_26);
  and and_25 (A_sltiu, operation, in_27);
  and and_26 (A_blez, operation, in_29);
  and and_27 (A_mult, operation, in_30);
  and and_28 (A_slt, operation, in_32);
  and and_29 (A_nor, operation, in_34);
  and and_30 (out_44, operation, in_35);
  and and_31 (A_andi, operation, in_37);
  and and_32 (A_bgtz, operation, in_39);
  Priority_Encoder #(.select(4)) priority_encoder_1 (
    .in0(or_7_out), .in1(in_22), .in2(in_30), .in3(in_14), .in4(or_4_out), .in5(in_34), .in6(or_8_out),
    .in7(or_5_out), .in8(or_9_out), .in9(in_2), .in10(in_23), .in11(or_6_out), .out(priority_encoder_1_out));  // open: in12, in13, in14, in15, gs, en_out, en_in
  nor nor_1 (nor_1_out, or_7_out, in_22, in_30, in_14, or_4_out, in_34, or_5_out, or_9_out, in_2, in_23, or_8_out, or_6_out);
  Multiplexer #(.width(4), .enable("false")) multiplexer_1 (
    .in0(priority_encoder_1_out), .in1(4'b0000), .out(ALU_op), .sel(nor_1_out));
  or or_10 (stack_flag, in_16, in_5);
  or or_11 (or_11_out, demultiplexer_1_out0, out_46);
  Demultiplexer #(.enable("false")) demultiplexer_1 (
    .out0(demultiplexer_1_out0), .out1(demultiplexer_1_out1), .in(d_ff_1_q), .sel(or_12_out));
  D_Flip_Flop d_ff_1 (.clk(in_36), .D(or_11_out), .Q(d_ff_1_q), .Qn(d_ff_1_qn), .preset(d_ff_1_qn));  // open: en, reset
  or or_12 (or_12_out, in_31, in_33);
  or or_13 (out_40, A_lw, A_pop);
  or or_14 (out_41, A_sw, A_push);
  nand nand_1 (nand_1_out, in_16, ~in_33);  // NAND_Gate
  and and_33 (and_33_out, in_5, in_33);
  and and_34 (and_34_out, ~in_33, in_31);  // AND_Gate
  and and_35 (operation, demultiplexer_1_out1, ~in_33);  // AND_Gate
  or or_15 (or_15_out, nand_1_out, and_33_out);
  and and_36 (and_36_out, and_34_out, in_5);
  Multiplexer #(.enable("false")) multiplexer_2 (
    .in0(undriven), .in1(or_15_out), .out(pop_push_flag), .sel(stack_flag));
  or or_16 (or_16_out, A_bgtz, A_andi, out_44, A_nor, A_slt, A_mult, A_blez, A_sltiu, out_55, A_mflo, A_divu, A_sub, A_bne, A_xori, A_slti, A_or, A_nop, A_mulu, A_sltu, A_xor, A_jr, out_45, A_addi, A_ori, A_beq, A_bltz, A_jump, A_add, A_div, A_and, A_mfhi, out_43);
  or or_17 (out_46, and_36_out, or_16_out, and_37_out);
  and and_37 (and_37_out, in_33, in_16);
  and and_38 (enable_push, operation, in_16);
  and and_39 (and_39_out, ~A_push, enable_push);  // AND_Gate
  or or_18 (out_42, A_sub, A_sltu, A_mulu, A_xor, A_addi, A_ori, A_jr, A_add, A_div, A_and, A_mfhi, A_slti, A_xori, A_divu, A_or, A_mflo, out_55, A_sltiu, A_mult, A_slt, A_nor, out_44, A_andi, in_28, enable_pop, and_43_out);
  and and_40 (A_sw, operation, in_38);
  D_Flip_Flop d_ff_2 (.clk(in_36), .D(and_39_out), .Q(A_push));  // open: Qn, preset, en, reset
  and and_41 (A_lw, operation, in_28);
  and and_42 (A_pop, operation, in_5);
  and and_43 (and_43_out, in_16, A_push);
  and and_44 (enable_pop, in_5, in_33);

  // Other names for the same wires on the sheet: active_operation = out_46; add = in_13; addi = in_8; and = in_15;
  //   andi = in_37; beq = in_10; bgtz = in_39; blez = in_29; bltz = in_11; bne = in_21; clock = in_36; div = in_14;
  //   divu = in_23; En_Inst = out_54; en_pop = enable_pop; en_push = enable_push; halt = in_7;
  //   instruction_loaded = in_31; jr = in_6; jump = in_12; kbd = in_35; lw = in_28; mfhi = in_17; mflo = in_25;
  //   mult = in_30; mulu = in_2; nop = in_1; nor = in_34; or = in_24; ori = in_9; pop = in_5; push = in_16;
  //   A_kbd = out_44; R_kbd_flag = out_44; R_ram_flag = out_40; rnd = in_26; A_rnd = out_55; rnd_flag = out_55;
  //   slt = in_32; slti = in_19; sltiu = in_27; sltu = in_3; A_halt = out_45; stop_flag = out_45; sub = in_22;
  //   sw = in_38; tty = in_18; A_tty = out_43; tty_flag = out_43; W_ram_flag = out_41; W_RF_flag = out_42;
  //   write_read_finish = in_33; xor = in_4; xori = in_20
endmodule
