// Logisim project Register File.circ as structural Verilog: 1 circuit, main circuit Register File
module Register_File (
  input  [31:0] Input,
  input  [4:0] In_Selector,
  input  [4:0] Out1_Selector,
  input  Clock,
  input  [1:0] Hi_Lo_Instruction,
  input  [4:0] Out2_Selector,
  input  Reset,
  input  [1:0] Stack_Instruction,
  input  Read_Write,
  output [31:0] Get1,
  output [31:0] Get2,
  output [31:0] Get_Hi_Lo
);

  wire and_1_out, and_2_out, En0, En1, En2, En3, En4, En5, En6, En7, En8, En9, En10, En11, En12, En13, En14,
       En15, En16, En17, En18, En19, En20, En21, En22, En23, En24, En25, En26, En27, En28, En29, En30, En31;
  wire [31:0] adder_1_out, Hi_q, Lo_q, multiplexer_1_out, o0, o1, o2, o3, o4, o5, o6, o7, o8, o9, o10, o11,
       o12, o13, o14, o15, o16, o17, o18, o19, o20, o21, o22, o23, o24, o25, o26, o27, o28, o29, o30, sp;

  Register #(.width(32)) R0 (.D(Input), .en(En0), .Q(o0), .clk(Clock), .clr(Reset));
  Register #(.width(32)) R4 (.D(Input), .en(En4), .Q(o4), .clk(Clock), .clr(Reset));
  Register #(.width(32)) R8 (.D(Input), .en(En8), .Q(o8), .clk(Clock), .clr(Reset));
  Register #(.width(32)) R12 (.D(Input), .en(En12), .Q(o12), .clk(Clock), .clr(Reset));
  Register #(.width(32)) R16 (.D(Input), .en(En16), .Q(o16), .clk(Clock), .clr(Reset));
  Register #(.width(32)) R20 (.D(Input), .en(En20), .Q(o20), .clk(Clock), .clr(Reset));
  Register #(.width(32)) R24 (.D(Input), .en(En24), .Q(o24), .clk(Clock), .clr(Reset));
  Register #(.width(32)) R28 (.D(Input), .en(En28), .Q(o28), .clk(Clock), .clr(Reset));
  Register #(.width(32)) R1 (.D(Input), .en(En1), .Q(o1), .clk(Clock), .clr(Reset));
  Register #(.width(32)) R5 (.D(Input), .en(En5), .Q(o5), .clk(Clock), .clr(Reset));
  Register #(.width(32)) R9 (.D(Input), .en(En9), .Q(o9), .clk(Clock), .clr(Reset));
  Register #(.width(32)) R13 (.D(Input), .en(En13), .Q(o13), .clk(Clock), .clr(Reset));
  Register #(.width(32)) R17 (.D(Input), .en(En17), .Q(o17), .clk(Clock), .clr(Reset));
  Register #(.width(32)) R21 (.D(Input), .en(En21), .Q(o21), .clk(Clock), .clr(Reset));
  Register #(.width(32)) R25 (.D(Input), .en(En25), .Q(o25), .clk(Clock), .clr(Reset));
  Register #(.width(32)) R29 (.D(Input), .en(En29), .Q(o29), .clk(Clock), .clr(Reset));
  Register #(.width(32)) R2 (.D(Input), .en(En2), .Q(o2), .clk(Clock), .clr(Reset));
  Register #(.width(32)) R6 (.D(Input), .en(En6), .Q(o6), .clk(Clock), .clr(Reset));
  Register #(.width(32)) R10 (.D(Input), .en(En10), .Q(o10), .clk(Clock), .clr(Reset));
  Register #(.width(32)) R14 (.D(Input), .en(En14), .Q(o14), .clk(Clock), .clr(Reset));
  Register #(.width(32)) R18 (.D(Input), .en(En18), .Q(o18), .clk(Clock), .clr(Reset));
  Register #(.width(32)) R22 (.D(Input), .en(En22), .Q(o22), .clk(Clock), .clr(Reset));
  Register #(.width(32)) R26 (.D(Input), .en(En26), .Q(o26), .clk(Clock), .clr(Reset));
  Register #(.width(32)) R30 (.D(Input), .en(En30), .Q(o30), .clk(Clock), .clr(Reset));
  Multiplexer #(.width(32), .enable("false")) multiplexer_1 (
    .in0(32'hfffffffc), .in1(32'h4), .out(multiplexer_1_out), .sel(Stack_Instruction[0]));
  Register #(.width(32)) R3 (.D(Input), .en(En3), .Q(o3), .clk(Clock), .clr(Reset));
  Register #(.width(32)) R7 (.D(Input), .en(En7), .Q(o7), .clk(Clock), .clr(Reset));
  Register #(.width(32)) R11 (.D(Input), .en(En11), .Q(o11), .clk(Clock), .clr(Reset));
  Register #(.width(32)) R15 (.D(Input), .en(En15), .Q(o15), .clk(Clock), .clr(Reset));
  Register #(.width(32)) R19 (.D(Input), .en(En19), .Q(o19), .clk(Clock), .clr(Reset));
  Register #(.width(32)) R23 (.D(Input), .en(En23), .Q(o23), .clk(Clock), .clr(Reset));
  Register #(.width(32)) R27 (.D(Input), .en(En27), .Q(o27), .clk(Clock), .clr(Reset));
  Adder #(.width(32)) adder_1 (.a(multiplexer_1_out), .b(sp), .out(adder_1_out));  // open: cin, cout
  Register #(.width(32)) R31 (.D(adder_1_out), .en(Stack_Instruction[1]), .Q(sp), .clk(Clock), .clr(Reset));
  Multiplexer #(.select(5), .enable("false")) multiplexer_2 (
    .in0(En0), .in1(En1), .in2(En2), .in3(En3), .in4(En4), .in5(En5), .in6(En6), .in7(En7), .in8(En8),
    .in9(En9), .in10(En10), .in11(En11), .in12(En12), .in13(En13), .in14(En14), .in15(En15), .in16(En16),
    .in17(En17), .in18(En18), .in19(En19), .in20(En20), .in21(En21), .in22(En22), .in23(En23), .in24(En24),
    .in25(En25), .in26(En26), .in27(En27), .in28(En28), .in29(En29), .in30(En30), .in31(En31),
    .out(Read_Write), .sel(In_Selector));
  and and_1 (and_1_out, Hi_Lo_Instruction[0], Hi_Lo_Instruction[1]);
  and and_2 (and_2_out, Hi_Lo_Instruction[0], ~Hi_Lo_Instruction[1]);  // AND_Gate
  Register #(.width(32)) Hi (.D(Input), .en(and_1_out), .Q(Hi_q), .clk(Clock), .clr(Reset));
  Register #(.width(32)) Lo (.D(Input), .en(and_2_out), .Q(Lo_q), .clk(Clock), .clr(Reset));
  Multiplexer #(.width(32), .enable("false")) multiplexer_3 (
    .in0(Lo_q), .in1(Hi_q), .out(Get_Hi_Lo), .sel(Hi_Lo_Instruction[1]));
  Demultiplexer #(.select(5), .width(32), .enable("false")) demultiplexer_1 (
    .out0(o0), .out1(o1), .out2(o2), .out3(o3), .out4(o4), .out5(o5), .out6(o6), .out7(o7), .out8(o8),
    .out9(o9), .out10(o10), .out11(o11), .out12(o12), .out13(o13), .out14(o14), .out15(o15), .out16(o16),
    .out17(o17), .out18(o18), .out19(o19), .out20(o20), .out21(o21), .out22(o22), .out23(o23), .out24(o24),
    .out25(o25), .out26(o26), .out27(o27), .out28(o28), .out29(o29), .out30(o30), .out31(sp), .in(Get1),
    .sel(Out1_Selector));
  Demultiplexer #(.select(5), .width(32), .enable("false")) demultiplexer_2 (
    .out0(o0), .out1(o1), .out2(o2), .out3(o3), .out4(o4), .out5(o5), .out6(o6), .out7(o7), .out8(o8),
    .out9(o9), .out10(o10), .out11(o11), .out12(o12), .out13(o13), .out14(o14), .out15(o15), .out16(o16),
    .out17(o17), .out18(o18), .out19(o19), .out20(o20), .out21(o21), .out22(o22), .out23(o23), .out24(o24),
    .out25(o25), .out26(o26), .out27(o27), .out28(o28), .out29(o29), .out30(o30), .out31(sp), .in(Get2),
    .sel(Out2_Selector));

  // Other names for the same wires on the sheet: Clk = Clock; H_L_select[1:0] = Hi_Lo_Instruction; in[31:0] = Input;
  //   r_w = Read_Write; Stack_select[1:0] = Stack_Instruction

  // Notes on the sheet:
  //   Registers
  //   Register Enable
  //   Register Out1
  //   Register Out2
endmodule
